// Logisim project Computerception.circ as structural Verilog: 17 circuits, main circuit FullAdder
module main (
  input  rst
);

  wire buffer_1_out, clk, not_1_out, or_1_out, ramLoad, ramLoadGPU, ramStore;
  wire [11:0] nextLine;
  wire [15:0] CPUadress, GPUadress, ramAdress, ramData, ramOut, romOut;
  wire [31:0] displayprocessor_1_out_8, displayprocessor_1_out_9, displayprocessor_1_out_10,
       displayprocessor_1_out_11, displayprocessor_1_out_12, displayprocessor_1_out_13,
       displayprocessor_1_out_14, displayprocessor_1_out_15, displayprocessor_1_out_16,
       displayprocessor_1_out_17, displayprocessor_1_out_18, displayprocessor_1_out_19,
       displayprocessor_1_out_20, displayprocessor_1_out_21, displayprocessor_1_out_22,
       displayprocessor_1_out_23, displayprocessor_1_out_24, displayprocessor_1_out_25,
       displayprocessor_1_out_26, displayprocessor_1_out_27, displayprocessor_1_out_28,
       displayprocessor_1_out_29, displayprocessor_1_out_30, displayprocessor_1_out_31,
       displayprocessor_1_out_32, displayprocessor_1_out_33, displayprocessor_1_out_34,
       displayprocessor_1_out_35, displayprocessor_1_out_36, displayprocessor_1_out_37,
       displayprocessor_1_out_38, displayprocessor_1_out_39;

  Clock u_clk (.out(clk));
  buf buffer_1 (buffer_1_out, rst);
  // Probe on ramAdress
  Processador processador_1 (
    .in_1(romOut), .clk(clk), .rst(rst), .NextLine(nextLine), .out_4(CPUadress), .out_5(ramData),
    .out_6(ramStore), .out_8(ramLoad));
  RAM ram_1 (
    .in_1(ramAdress), .in_2(ramData), .out_7(ramOut), .in_4(ramStore), .in_5(clk), .in_3(or_1_out), .in_6(rst));
  // Probe on ramData
  // Probe on ramOut
  or or_1 (or_1_out, ramLoadGPU, ramLoad);
  ROM #(.addrWidth(12), .dataWidth(16)) rom_1 (.addr(nextLine), .data(romOut));  // open: sel
  // Probe on displayprocessor_1_out_8
  DotMatrix #(.matrixcols(32), .matrixrows(32), .persist(128)) dotmatrix_1 (
    .col0(displayprocessor_1_out_8), .col1(displayprocessor_1_out_9), .col2(displayprocessor_1_out_10),
    .col3(displayprocessor_1_out_11), .col4(displayprocessor_1_out_12), .col5(displayprocessor_1_out_13),
    .col6(displayprocessor_1_out_14), .col7(displayprocessor_1_out_15), .col8(displayprocessor_1_out_16),
    .col9(displayprocessor_1_out_17), .col10(displayprocessor_1_out_18), .col11(displayprocessor_1_out_19),
    .col12(displayprocessor_1_out_20), .col13(displayprocessor_1_out_21), .col14(displayprocessor_1_out_22),
    .col15(displayprocessor_1_out_23), .col16(displayprocessor_1_out_24), .col17(displayprocessor_1_out_25),
    .col18(displayprocessor_1_out_26), .col19(displayprocessor_1_out_27), .col20(displayprocessor_1_out_28),
    .col21(displayprocessor_1_out_29), .col22(displayprocessor_1_out_30), .col23(displayprocessor_1_out_31),
    .col24(displayprocessor_1_out_32), .col25(displayprocessor_1_out_33), .col26(displayprocessor_1_out_34),
    .col27(displayprocessor_1_out_35), .col28(displayprocessor_1_out_36), .col29(displayprocessor_1_out_37),
    .col30(displayprocessor_1_out_38), .col31(displayprocessor_1_out_39));
  DisplayProcessor displayprocessor_1 (
    .Store(ramStore), .Load(ramLoad), .Reset(rst), .dataIn(ramOut), .GetData(ramLoadGPU),
    .RegAdress(GPUadress), .out_8(displayprocessor_1_out_8), .out_24(displayprocessor_1_out_24),
    .out_9(displayprocessor_1_out_9), .out_25(displayprocessor_1_out_25), .out_10(displayprocessor_1_out_10),
    .out_26(displayprocessor_1_out_26), .out_11(displayprocessor_1_out_11),
    .out_27(displayprocessor_1_out_27), .out_12(displayprocessor_1_out_12),
    .out_28(displayprocessor_1_out_28), .out_13(displayprocessor_1_out_13),
    .out_29(displayprocessor_1_out_29), .out_14(displayprocessor_1_out_14),
    .out_30(displayprocessor_1_out_30), .out_15(displayprocessor_1_out_15),
    .out_31(displayprocessor_1_out_31), .out_16(displayprocessor_1_out_16),
    .out_32(displayprocessor_1_out_32), .out_17(displayprocessor_1_out_17),
    .out_33(displayprocessor_1_out_33), .out_18(displayprocessor_1_out_18),
    .out_34(displayprocessor_1_out_34), .out_19(displayprocessor_1_out_19),
    .out_35(displayprocessor_1_out_35), .out_20(displayprocessor_1_out_20),
    .out_36(displayprocessor_1_out_36), .out_21(displayprocessor_1_out_21),
    .out_37(displayprocessor_1_out_37), .out_22(displayprocessor_1_out_22),
    .out_38(displayprocessor_1_out_38), .out_23(displayprocessor_1_out_23),
    .out_39(displayprocessor_1_out_39), .clk(clk));
  not not_1 (not_1_out, ramLoadGPU);
  Transistor #(.width(16)) transistor_1 (.in(GPUadress), .out(ramAdress), .gate(not_1_out));
  Transistor #(.width(16)) transistor_2 (.in(CPUadress), .out(ramAdress), .gate(ramLoadGPU));
  // Probe on GPUadress

  // Notes on the sheet:
  //   contents of rom_1 (hex, n*v repeats v):
  //   2010 2108 1901 2240 1402 2310 1931 1b30 3230 213f 1431 3230 600c
endmodule

module FullAdder (
  input  a,
  input  b,
  input  ci,
  output s,
  output co
);

  wire halfsum_1_c, halfsum_1_s, halfsum_2_c;

  HalfSum halfsum_1 (.a(a), .b(b), .s(halfsum_1_s), .c(halfsum_1_c));
  HalfSum halfsum_2 (.a(halfsum_1_s), .b(ci), .s(s), .c(halfsum_2_c));
  or or_1 (co, halfsum_2_c, halfsum_1_c);
endmodule

module HalfSum (
  input  a,
  input  b,
  output s,
  output c
);

  xor xor_1 (s, a, b);
  and and_1 (c, a, b);
endmodule

module _4_bit_Ripple_Carry_Adder (
  input  ci,
  input  b0,
  input  b1,
  input  b2,
  input  b3,
  input  a0,
  input  a1,
  input  a2,
  input  a3,
  output s0,
  output s1,
  output s2,
  output s3,
  output co
);

  wire fulladder_1_co, fulladder_2_co, fulladder_3_co;

  LED led_1 (.in(s0));
  FullAdder fulladder_1 (.a(a0), .b(b0), .ci(ci), .s(s0), .co(fulladder_1_co));
  LED led_2 (.in(s1));
  FullAdder fulladder_2 (.a(a1), .b(b1), .ci(fulladder_1_co), .s(s1), .co(fulladder_2_co));
  LED led_3 (.in(s2));
  FullAdder fulladder_3 (.a(a2), .b(b2), .ci(fulladder_2_co), .s(s2), .co(fulladder_3_co));
  FullAdder fulladder_4 (.a(a3), .b(b3), .ci(fulladder_3_co), .s(s3), .co(co));
  LED led_4 (.in(s3));
  LED led_5 (.in(co));

  // Notes on the sheet:
  //   1
  //   1
  //   1
  //   2
  //   4
  //   2
  //   4
  //   2
  //   8
  //   8
  //   4
  //   8
  //   16
endmodule

module _4_bit_wirh_splitter (
  input  [3:0] in_1,
  input  [3:0] in_2,
  input  in_3,
  output [4:0] out_4
);

  wire fulladder_2_co, fulladder_3_co, fulladder_4_co;

  FullAdder fulladder_1 (.a(in_2[3]), .b(in_1[3]), .ci(fulladder_3_co), .s(out_4[3]), .co(out_4[4]));
  FullAdder fulladder_2 (.a(in_2[1]), .b(in_1[1]), .ci(fulladder_4_co), .s(out_4[1]), .co(fulladder_2_co));
  FullAdder fulladder_3 (.a(in_2[2]), .b(in_1[2]), .ci(fulladder_2_co), .s(out_4[2]), .co(fulladder_3_co));
  FullAdder fulladder_4 (.a(in_2[0]), .b(in_1[0]), .ci(in_3), .s(out_4[0]), .co(fulladder_4_co));
endmodule

module _8_bit_adder (
  input  [7:0] in_1,
  input  [7:0] in_2,
  input  ci,
  output c0,
  output [7:0] out_5
);

  wire n4_bit_ripple_carry_adder_2_co;

  _4_bit_Ripple_Carry_Adder u_4_bit_ripple_carry_adder_1 (
    .ci(n4_bit_ripple_carry_adder_2_co), .b0(in_2[4]), .a0(in_1[4]), .b1(in_2[5]), .a1(in_1[5]),
    .b2(in_1[6]), .a2(in_2[6]), .b3(in_2[7]), .a3(in_1[7]), .s0(out_5[4]), .s1(out_5[5]), .s2(out_5[6]),
    .s3(out_5[7]), .co(c0));
  // Probe on in_1
  // Probe on in_2
  _4_bit_Ripple_Carry_Adder u_4_bit_ripple_carry_adder_2 (
    .ci(ci), .b0(in_2[0]), .a0(in_1[0]), .b1(in_2[1]), .a1(in_1[1]), .b2(in_2[2]), .a2(in_1[2]),
    .b3(in_2[3]), .a3(in_1[3]), .s0(out_5[0]), .s1(out_5[1]), .s2(out_5[2]), .s3(out_5[3]),
    .co(n4_bit_ripple_carry_adder_2_co));
  // Probe on out_5
endmodule

module _16_bit_adder (
  input  [15:0] in_1,
  input  [15:0] in_2,
  input  ci,
  output co,
  output [15:0] out_5
);

  wire n8_bit_adder_2_c0;

  // Probe on in_1
  _8_bit_adder u_8_bit_adder_1 (
    .in_1(in_2[15:8]), .in_2(in_1[15:8]), .c0(co), .ci(n8_bit_adder_2_c0), .out_5(out_5[15:8]));
  // Probe on out_5
  // Probe on in_2
  _8_bit_adder u_8_bit_adder_2 (
    .in_1(in_2[7:0]), .in_2(in_1[7:0]), .c0(n8_bit_adder_2_c0), .ci(ci), .out_5(out_5[7:0]));
endmodule

module _32_bit_adder (
  input  [31:0] in_1,
  input  [31:0] in_2,
  input  ci,
  output co,
  output [31:0] out_5
);

  wire n16_bit_adder_2_co;

  // Probe on in_1
  _16_bit_adder u_16_bit_adder_1 (
    .in_1(in_2[31:16]), .in_2(in_1[31:16]), .out_5(out_5[31:16]), .ci(n16_bit_adder_2_co), .co(co));
  // Probe on out_5
  _16_bit_adder u_16_bit_adder_2 (
    .in_1(in_2[15:0]), .in_2(in_1[15:0]), .out_5(out_5[15:0]), .ci(ci), .co(n16_bit_adder_2_co));
  // Probe on in_2
endmodule

module SR_Latch (
  input  S,
  input  R,
  output Q_prime
);

  wire not_2_out, or_1_out, or_2_out;

  or or_1 (or_1_out, S, not_2_out);
  not not_1 (Q_prime, or_1_out);
  or or_2 (or_2_out, Q_prime, R);
  not not_2 (not_2_out, or_2_out);
endmodule

module D_Latch (
  input  Data,
  input  Enable,
  output Q
);

  wire and_1_out, and_2_out, not_1_out, not_2_out, not_3_out;

  not not_1 (not_1_out, Data);
  and and_1 (and_1_out, Data, Enable);
  and and_2 (and_2_out, Enable, not_1_out);
  not not_2 (not_2_out, and_1_out);
  SR_Latch sr_latch_1 (.S(not_2_out), .R(not_3_out), .Q_prime(Q));
  not not_3 (not_3_out, and_2_out);
endmodule

module Aula2 (
  input  in_1,
  input  in_2,
  input  in_3,
  input  in_4,
  input  in_5,
  input  in_6,
  input  in_7,
  input  in_8,
  input  in_9,
  input  in_10,
  input  in_11,
  input  in_12,
  output out_13,
  output out_14,
  output out_15,
  output out_16,
  output out_17,
  output out_18,
  output out_19,
  output out_20,
  output out_21,
  output Q,
  output out_23,
  output Q_prime
);

  wire and_1_out, and_2_out, and_3_out, and_4_out, and_5_out, and_6_out, and_7_out, and_8_out, and_9_out,
       and_10_out, and_11_out, and_12_out, not_1_out, not_8_out, not_9_out, not_10_out, not_11_out,
       not_12_out, not_13_out, or_1_out, or_2_out, or_3_out, or_4_out, or_5_out, or_6_out;

  and and_1 (and_1_out, in_2, out_15);
  and and_2 (and_2_out, out_13, in_4);
  or or_1 (or_1_out, in_6, out_19);
  or or_2 (or_2_out, out_17, in_8);
  not not_1 (not_1_out, in_9);
  or or_3 (or_3_out, not_1_out, out_23);
  or or_4 (or_4_out, out_21, in_9);
  Clock clock_1 ();  // open: out
  not not_2 (out_13, and_1_out);
  not not_3 (out_15, and_2_out);
  not not_4 (out_17, or_1_out);
  not not_5 (out_19, or_2_out);
  not not_6 (out_21, or_3_out);
  not not_7 (out_23, or_4_out);
  not not_8 (not_8_out, in_1);
  not not_9 (not_9_out, in_5);
  and and_3 (and_3_out, in_1, in_3);
  not not_10 (not_10_out, and_3_out);
  not not_11 (not_11_out, and_4_out);
  and and_4 (and_4_out, in_3, not_8_out);
  and and_5 (and_5_out, in_5, in_7);
  and and_6 (and_6_out, in_7, not_9_out);
  not not_12 (not_12_out, and_7_out);
  and and_7 (and_7_out, Q_prime, in_10, in_11);
  not not_13 (not_13_out, and_8_out);
  and and_8 (and_8_out, in_11, in_12, Q);
  and and_9 (and_9_out, not_10_out, out_16);
  and and_10 (and_10_out, out_14, not_11_out);
  or or_5 (or_5_out, and_5_out, out_20);
  not not_14 (out_18, or_5_out);
  or or_6 (or_6_out, out_18, and_6_out);
  not not_15 (out_20, or_6_out);
  and and_11 (and_11_out, not_12_out, Q_prime);
  and and_12 (and_12_out, Q, not_13_out);
  not not_16 (out_14, and_9_out);
  not not_17 (out_16, and_10_out);
  not not_18 (Q, and_11_out);
  not not_19 (Q_prime, and_12_out);
endmodule

module SR_Flip_Flop (
  input  D,
  input  Enable,
  input  Clock,
  output Q
);

  wire and_1_out, d_latch_1_q, not_1_out;

  and and_1 (and_1_out, Enable, Clock);
  D_Latch d_latch_1 (.Data(D), .Enable(and_1_out), .Q(d_latch_1_q));
  not not_1 (not_1_out, Clock);
  D_Latch d_latch_2 (.Data(d_latch_1_q), .Enable(not_1_out), .Q(Q));
endmodule

module Registrador (
  input  Clock,
  input  Enable,
  input  Reset,
  input  [3:0] AdressA,
  input  [3:0] AdressB,
  input  [15:0] Data,
  output [15:0] DataA,
  output [15:0] DataB
);

  wire clk, clock_1_out, en0, en1, en2, en3, en4, en5, en6, en7, en8, en9, en10, en11, en12, en13, en14, en15;
  wire [15:0] out0, out1, out2, out3, out4, out5, out6, out7, out8, out9, out10, out11, out12, out13, out14,
       out15;

  Clock clock_1 (.out(clock_1_out));
  or or_1 (clk, clock_1_out, Clock);
  Register #(.width(16)) register_1 (.D(Data), .en(en0), .Q(out0), .clk(clk), .clr(Reset));
  Register #(.width(16)) register_2 (.D(Data), .en(en4), .Q(out4), .clk(clk), .clr(Reset));
  Register #(.width(16)) register_3 (.D(Data), .en(en8), .Q(out8), .clk(clk), .clr(Reset));
  Register #(.width(16)) register_4 (.D(Data), .en(en12), .Q(out12), .clk(clk), .clr(Reset));
  Demultiplexer #(.select(4)) demultiplexer_1 (
    .out0(en0), .out1(en1), .out2(en2), .out3(en3), .out4(en4), .out5(en5), .out6(en6), .out7(en7),
    .out8(en8), .out9(en9), .out10(en10), .out11(en11), .out12(en12), .out13(en13), .out14(en14),
    .out15(en15), .in(Enable), .sel(AdressA));  // open: en
  Register #(.width(16)) register_5 (.D(Data), .en(en1), .Q(out1), .clk(clk), .clr(Reset));
  Register #(.width(16)) register_6 (.D(Data), .en(en5), .Q(out5), .clk(clk), .clr(Reset));
  Register #(.width(16)) register_7 (.D(Data), .en(en9), .Q(out9), .clk(clk), .clr(Reset));
  Register #(.width(16)) register_8 (.D(Data), .en(en13), .Q(out13), .clk(clk), .clr(Reset));
  Register #(.width(16)) register_9 (.D(Data), .en(en2), .Q(out2), .clk(clk), .clr(Reset));
  Register #(.width(16)) register_10 (.D(Data), .en(en6), .Q(out6), .clk(clk), .clr(Reset));
  Register #(.width(16)) register_11 (.D(Data), .en(en10), .Q(out10), .clk(clk), .clr(Reset));
  Register #(.width(16)) register_12 (.D(Data), .en(en14), .Q(out14), .clk(clk), .clr(Reset));
  Multiplexer #(.select(4), .width(16)) multiplexer_1 (
    .in0(out0), .in1(out1), .in2(out2), .in3(out3), .in4(out4), .in5(out5), .in6(out6), .in7(out7),
    .in8(out8), .in9(out9), .in10(out10), .in11(out11), .in12(out12), .in13(out13), .in14(out14),
    .in15(out15), .out(DataA), .sel(AdressA));  // open: en
  Register #(.width(16)) register_13 (.D(Data), .en(en3), .Q(out3), .clk(clk), .clr(Reset));
  Register #(.width(16)) register_14 (.D(Data), .en(en7), .Q(out7), .clk(clk), .clr(Reset));
  Register #(.width(16)) register_15 (.D(Data), .en(en11), .Q(out11), .clk(clk), .clr(Reset));
  Register #(.width(16)) register_16 (.D(Data), .en(en15), .Q(out15), .clk(clk), .clr(Reset));
  Multiplexer #(.select(4), .width(16)) multiplexer_2 (
    .in0(out0), .in1(out1), .in2(out2), .in3(out3), .in4(out4), .in5(out5), .in6(out6), .in7(out7),
    .in8(out8), .in9(out9), .in10(out10), .in11(out11), .in12(out12), .in13(out13), .in14(out14),
    .in15(out15), .out(DataB), .sel(AdressB));  // open: en

  // Other names for the same wires on the sheet: rst = Reset
endmodule

module ULA (
  input  [15:0] in_1,
  input  [15:0] in_2,
  input  [3:0] BitSelector,
  output [15:0] Out,
  output [1:0] C
);

  wire comparator_1_eq, comparator_1_gt, comparator_1_lt;
  wire [15:0] And, Complet, Dec, DivOut, Inc, LeftShift, MinusOut, MultOut, Not, Or, RigthShift, Squared,
       SumOut, Xor;

  Multiplier #(.width(16)) multiplier_1 (.a(in_1), .b(in_2), .out(MultOut));  // open: cin, cout
  Adder #(.width(16)) adder_1 (.a(in_1), .b(in_2), .out(SumOut));  // open: cin, cout
  Divider #(.width(16)) divider_1 (.a(in_1), .b(in_2), .out(DivOut));  // open: upper, rem
  Multiplier #(.width(16)) multiplier_2 (.a(in_1), .b(in_1), .out(Squared));  // open: cin, cout
  assign And = in_1 & in_2;  // AND_Gate and_1, 16 bits wide
  assign Or = in_1 | in_2;  // OR_Gate or_1, 16 bits wide
  assign Not = ~in_1;  // NOT_Gate not_1, 16 bits wide
  assign Xor = in_1 ^ in_2;  // XOR_Gate xor_1, 16 bits wide
  Comparator #(.width(16)) comparator_1 (
    .a(in_1), .b(in_2), .gt(comparator_1_gt), .eq(comparator_1_eq), .lt(comparator_1_lt));
  or or_2 (C[0], comparator_1_gt, comparator_1_eq);
  or or_3 (C[1], comparator_1_eq, comparator_1_lt);
  Negator #(.width(16)) negator_1 (.in(in_1), .out(Complet));
  Shifter #(.width(16)) shifter_1 (.in(in_1), .\dist (in_2[3:0]), .out(LeftShift));
  Shifter #(.width(16), .shift("lr")) shifter_2 (.in(in_1), .\dist (in_2[3:0]), .out(RigthShift));
  Adder #(.width(16)) adder_2 (.a(in_1), .b(16'h1), .out(Inc));  // open: cin, cout
  Subtractor #(.width(16)) subtractor_1 (.a(in_1), .b(16'h1), .out(Dec));  // open: bin, bout
  Multiplexer #(.select(4), .width(16)) multiplexer_1 (
    .in0(And), .in1(Or), .in2(Not), .in3(Xor), .in4(SumOut), .in5(MinusOut), .in6(MultOut), .in7(DivOut),
    .in8(Complet), .in9(LeftShift), .in10(RigthShift), .in11(Inc), .in12(Dec), .out(Out), .sel(BitSelector));  // open: in13, in14, in15, en
  // Probe on Out

  // Other names for the same wires on the sheet: a[15:0] = in_1; b[15:0] = in_2
endmodule

module Processador (
  input  [15:0] in_1,
  input  clk,
  input  rst,
  output [15:0] out_4,
  output [15:0] out_5,
  output out_6,
  output [11:0] NextLine,
  output out_8
);

  wire and_13_out, and_14_out, and_16_out, and_17_out, and_18_out, and_19_out, and_20_out, and_21_out,
       and_22_out, and_23_out, CmpAB, CmpAC, DifMov, ISCmp, ISJmp, ISmov, ISMovI, ISop, ISPush, Je, Jg, Jge,
       Jne, Movl0000, MovRAM, or_1_out, or_3_out, regen;
  wire [1:0] LastCmp, ula_1_c;
  wire [3:0] A;
  wire [11:0] adder_1_out, next;
  wire [15:0] adder_2_out, data, multiplexer_2_out, multiplexer_5_out, multiplexer_8_out, NextPointer,
       Pointer, ramOut, regAout, subtractor_1_out, ulaBin, ULAOut;

  Register #(.width(12)) PC (.D(next), .Q(NextLine), .clk(clk), .clr(rst));  // open: en
  and and_1 (ISop, in_1[12], ~in_1[13], ~in_1[14], ~in_1[15]);  // AND_Gate
  and and_2 (ISmov, ~in_1[12], in_1[13], ~in_1[14], ~in_1[15]);  // AND_Gate
  and and_3 (ISCmp, ~in_1[12], ~in_1[13], in_1[14], ~in_1[15]);  // AND_Gate
  and and_4 (ISMovI, in_1[12], in_1[13], ~in_1[14], ~in_1[15]);  // AND_Gate
  and and_5 (Movl0000, ~in_1[8], ~in_1[9], ~in_1[10], ~in_1[11]);  // AND_Gate
  and and_6 (CmpAB, ~in_1[12], ~in_1[13], in_1[14], ~in_1[15]);  // AND_Gate
  and and_7 (CmpAC, in_1[12], ~in_1[13], in_1[14], ~in_1[15]);  // AND_Gate
  and and_8 (Je, in_1[12], in_1[13], in_1[14], ~in_1[15]);  // AND_Gate
  and and_9 (Jne, ~in_1[12], ~in_1[13], ~in_1[14], in_1[15]);  // AND_Gate
  and and_10 (Jg, in_1[12], ~in_1[13], ~in_1[14], in_1[15]);  // AND_Gate
  and and_11 (Jge, ~in_1[12], in_1[13], ~in_1[14], in_1[15]);  // AND_Gate
  buf and_12 (ISPush, ~in_1[10]);  // AND_Gate AND_Gate
  Adder #(.width(12)) adder_1 (.a(NextLine), .b(12'h1), .out(adder_1_out));  // open: cin, cout
  // Probe on regAout
  Registrador registrador_1 (
    .Clock(clk), .Enable(regen), .Reset(rst), .AdressA(A), .AdressB(in_1[3:0]), .Data(data), .DataB(out_5),
    .DataA(regAout));
  // Probe on out_5
  Multiplexer #(.width(12)) multiplexer_1 (.in0(adder_1_out), .in1(in_1[11:0]), .out(next), .sel(ISJmp));  // open: en
  and and_13 (and_13_out, Je, LastCmp[0], LastCmp[1]);
  and and_14 (and_14_out, Jne, ~LastCmp[0], ~LastCmp[1]);  // AND_Gate
  not not_1 (DifMov, Movl0000);
  and and_15 (MovRAM, DifMov, ISMovI);
  Register #(.width(16)) StackPointer (.D(multiplexer_2_out), .Q(Pointer), .clk(rst));  // open: en, clr
  Multiplexer #(.width(16)) multiplexer_2 (
    .in0(NextPointer), .in1({16{1'b1}}), .out(multiplexer_2_out), .sel(rst));  // open: en
  Subtractor #(.width(16)) subtractor_1 (.a(Pointer), .b(16'h1), .out(subtractor_1_out));  // open: bin, bout
  Adder #(.width(16)) adder_2 (.a(Pointer), .b(16'h1), .out(adder_2_out));  // open: cin, cout
  and and_16 (and_16_out, ~in_1[12], in_1[13], in_1[14], ~in_1[15]);  // AND_Gate
  and and_17 (and_17_out, Jg, LastCmp[0], ~LastCmp[1]);  // AND_Gate
  and and_18 (and_18_out, LastCmp[0], ~LastCmp[1]);  // AND_Gate
  or or_1 (or_1_out, and_18_out, and_19_out);
  and and_19 (and_19_out, LastCmp[0], LastCmp[1]);
  Multiplexer #(.width(16)) multiplexer_3 (
    .in0(subtractor_1_out), .in1(adder_2_out), .out(NextPointer));  // open: sel, en
  or or_2 (ISJmp, and_16_out, and_13_out, and_14_out, and_17_out, and_20_out);
  and and_20 (and_20_out, Jge, or_1_out);
  Multiplexer #(.width(4)) multiplexer_4 (.in0(in_1[3:0]), .in1(in_1[7:4]), .sel(out_6));  // open: out, en
  ULA ula_1 (.in_1(regAout), .in_2(ulaBin), .Out(ULAOut), .BitSelector(in_1[11:8]), .C(ula_1_c));
  and and_21 (and_21_out, ISMovI, ~out_6);  // AND_Gate
  Multiplexer #(.width(16)) multiplexer_5 (
    .in0(ULAOut), .in1({{8{1'b0}}, in_1[7:0]}), .out(multiplexer_5_out), .sel(ISmov));  // open: en
  // Probe on ULAOut
  Register #(.width(2)) register_1 (.D(ula_1_c), .en(or_3_out), .Q(LastCmp), .clk(clk), .clr(rst));
  or or_3 (or_3_out, CmpAB, CmpAC);
  Multiplexer #(.width(16)) multiplexer_6 (
    .in0(out_5), .in1({{8{1'b0}}, in_1[7:0]}), .out(ulaBin), .sel(CmpAC));  // open: en
  or or_4 (regen, ISop, and_21_out, ISmov, out_8);
  Multiplexer #(.width(16)) multiplexer_7 (.in0(out_5), .in1(regAout), .out(out_4), .sel(out_6));  // open: en
  Multiplexer #(.width(16)) multiplexer_8 (
    .in0(multiplexer_5_out), .in1(ramOut), .out(multiplexer_8_out), .sel(out_8));  // open: en
  Multiplexer #(.width(16)) multiplexer_9 (
    .in0(multiplexer_8_out), .in1(out_5), .out(data), .sel(and_22_out));  // open: en
  and and_22 (and_22_out, ISMovI, Movl0000);
  Multiplexer #(.width(4)) multiplexer_10 (.in0(in_1[7:4]), .in1(in_1[11:8]), .out(A), .sel(and_23_out));  // open: en
  and and_23 (and_23_out, ~ISCmp, ~MovRAM, ~ISop);  // AND_Gate
  and and_24 (out_6, MovRAM, ~in_1[8], in_1[9], ~in_1[10], ~in_1[11]);  // AND_Gate
  and and_25 (out_8, MovRAM, in_1[8], ~in_1[9], ~in_1[10], ~in_1[11]);  // AND_Gate
  // Probe on LastCmp

  // Other names for the same wires on the sheet: crr[11:0] = NextLine; inst[15:0] = in_1; Select[3:0] = in_1[15:12];
  //   B[3:0] = in_1[3:0]; C[7:0] = in_1[7:0]; l[11:0] = in_1[11:0]; s0[3:0] = in_1[3:0]; s1[3:0] = in_1[7:4];
  //   Op[3:0] = in_1[11:8]; s2[3:0] = in_1[11:8]; ramAdress[15:0] = out_4; ramLoad = out_8; ramStore = out_6;
  //   ramData[15:0] = out_5; regBout[15:0] = out_5; ulaAin[15:0] = regAout
endmodule

module RAM (
  input  [15:0] in_1,
  input  [15:0] in_2,
  input  in_3,
  input  in_4,
  input  in_5,
  input  in_6,
  output [15:0] out_7
);

  RAM_part #(.addrWidth(16), .dataWidth(16), .bus("separate")) ram_1 (
    .addr(in_1), .din(in_2), .data(out_7), .str(in_4), .clk(in_5), .ld(in_3), .clr(in_6));  // open: sel
endmodule

module DisplayProcessor (
  input  Store,
  input  Load,
  input  clk,
  input  Reset,
  input  [15:0] dataIn,
  output GetData,
  output [15:0] RegAdress,
  output [31:0] out_8,
  output [31:0] out_9,
  output [31:0] out_10,
  output [31:0] out_11,
  output [31:0] out_12,
  output [31:0] out_13,
  output [31:0] out_14,
  output [31:0] out_15,
  output [31:0] out_16,
  output [31:0] out_17,
  output [31:0] out_18,
  output [31:0] out_19,
  output [31:0] out_20,
  output [31:0] out_21,
  output [31:0] out_22,
  output [31:0] out_23,
  output [31:0] out_24,
  output [31:0] out_25,
  output [31:0] out_26,
  output [31:0] out_27,
  output [31:0] out_28,
  output [31:0] out_29,
  output [31:0] out_30,
  output [31:0] out_31,
  output [31:0] out_32,
  output [31:0] out_33,
  output [31:0] out_34,
  output [31:0] out_35,
  output [31:0] out_36,
  output [31:0] out_37,
  output [31:0] out_38,
  output [31:0] out_39
);

  wire clk_t, crrReg, demultiplexer_1_out0, demultiplexer_1_out1, eod, not_1_out, not_2_out, rst,
       transistor_1_out, transistor_2_out;
  wire [15:0] counter_1_q, register_1_q, register_2_q;
  wire [31:0] adder_1_out, bit_extender_1_out, bit_extender_2_out, shift_register_1_q0, shift_register_1_q1,
       shift_register_1_q2, shift_register_1_q3, shift_register_1_q4, shift_register_1_q5,
       shift_register_1_q6, shift_register_1_q7, shift_register_1_q8, shift_register_1_q9,
       shift_register_1_q10, shift_register_1_q11, shift_register_1_q12, shift_register_1_q13,
       shift_register_1_q14, shift_register_1_q15, shift_register_1_q16, shift_register_1_q17,
       shift_register_1_q18, shift_register_1_q19, shift_register_1_q20, shift_register_1_q21,
       shift_register_1_q22, shift_register_1_q23, shift_register_1_q24, shift_register_1_q25,
       shift_register_1_q26, shift_register_1_q27, shift_register_1_q28, shift_register_1_q29,
       shift_register_1_q30, shift_register_1_q31, shifter_1_out;

  or or_1 (rst, Reset, eod);
  nor nor_1 (GetData, Store, Load);
  and and_1 (clk_t, GetData, clk);
  T_Flip_Flop t_ff_1 (.clk(clk_t), .T(1'b1), .Q(crrReg), .reset(rst));  // open: Qn, preset, en
  not not_1 (not_1_out, crrReg);
  Counter #(.width(16), .max('hffff)) counter_1 (
    .Q(counter_1_q), .clk(clk_t), .clr(rst));  // open: load, D, count, carry
  Demultiplexer demultiplexer_1 (
    .out0(demultiplexer_1_out0), .out1(demultiplexer_1_out1), .in(not_2_out), .sel(crrReg));  // open: en
  not not_2 (not_2_out, clk_t);
  Counter #(.width(16), .max('hffff)) counter_2 (.clk(not_1_out), .clr(rst));  // open: load, D, count, Q, carry
  Subtractor #(.width(16)) subtractor_1 (.a(16'h1041), .b(counter_1_q), .out(RegAdress));  // open: bin, bout
  Comparator #(.width(16)) comparator_1 (.a(counter_1_q), .b(16'h43), .eq(eod));  // open: gt, lt
  // Probe on RegAdress
  Register #(.width(16), .trigger("falling")) register_1 (
    .D(dataIn), .Q(register_1_q), .clk(transistor_1_out), .clr(rst));  // open: en
  Transistor #(.gate("br")) transistor_1 (.in(demultiplexer_1_out0), .out(transistor_1_out), .gate(rst));
  Register #(.width(16), .trigger("falling")) register_2 (
    .D(dataIn), .Q(register_2_q), .clk(transistor_2_out), .clr(rst));  // open: en
  Transistor #(.gate("br")) transistor_2 (.in(demultiplexer_1_out1), .out(transistor_2_out), .gate(rst));
  Shift_Register #(.width(32), .length(32)) shift_register_1 (
    .in(adder_1_out), .clk(crrReg), .clr(rst), .q0(shift_register_1_q0), .q1(shift_register_1_q1),
    .q2(shift_register_1_q2), .q3(shift_register_1_q3), .q4(shift_register_1_q4), .q5(shift_register_1_q5),
    .q6(shift_register_1_q6), .q7(shift_register_1_q7), .q8(shift_register_1_q8), .q9(shift_register_1_q9),
    .q10(shift_register_1_q10), .q11(shift_register_1_q11), .q12(shift_register_1_q12),
    .q13(shift_register_1_q13), .q14(shift_register_1_q14), .q15(shift_register_1_q15),
    .q16(shift_register_1_q16), .q17(shift_register_1_q17), .q18(shift_register_1_q18),
    .q19(shift_register_1_q19), .q20(shift_register_1_q20), .q21(shift_register_1_q21),
    .q22(shift_register_1_q22), .q23(shift_register_1_q23), .q24(shift_register_1_q24),
    .q25(shift_register_1_q25), .q26(shift_register_1_q26), .q27(shift_register_1_q27),
    .q28(shift_register_1_q28), .q29(shift_register_1_q29), .q30(shift_register_1_q30),
    .q31(shift_register_1_q31));  // open: shift, out, load, d0, d1, d2, d3, d4, d5, d6, d7, d8, d9, d10, d11, d12, d13, d14, d15, d16, d17, d18, d19, d20, d21, d22, d23, d24, d25, d26, d27, d28, d29, d30, d31
  Shift_Register #(.width(32), .length(32)) shift_register_2 (
    .clk(eod), .load(1'b1), .clr(Reset), .d0(shift_register_1_q0), .q0(out_8), .d1(shift_register_1_q1),
    .q1(out_9), .d2(shift_register_1_q2), .q2(out_10), .d3(shift_register_1_q3), .q3(out_11),
    .d4(shift_register_1_q4), .q4(out_12), .d5(shift_register_1_q5), .q5(out_13), .d6(shift_register_1_q6),
    .q6(out_14), .d7(shift_register_1_q7), .q7(out_15), .d8(shift_register_1_q8), .q8(out_16),
    .d9(shift_register_1_q9), .q9(out_17), .d10(shift_register_1_q10), .q10(out_18),
    .d11(shift_register_1_q11), .q11(out_19), .d12(shift_register_1_q12), .q12(out_20),
    .d13(shift_register_1_q13), .q13(out_21), .d14(shift_register_1_q14), .q14(out_22),
    .d15(shift_register_1_q15), .q15(out_23), .d16(shift_register_1_q16), .q16(out_24),
    .d17(shift_register_1_q17), .q17(out_25), .d18(shift_register_1_q18), .q18(out_26),
    .d19(shift_register_1_q19), .q19(out_27), .d20(shift_register_1_q20), .q20(out_28),
    .d21(shift_register_1_q21), .q21(out_29), .d22(shift_register_1_q22), .q22(out_30),
    .d23(shift_register_1_q23), .q23(out_31), .d24(shift_register_1_q24), .q24(out_32),
    .d25(shift_register_1_q25), .q25(out_33), .d26(shift_register_1_q26), .q26(out_34),
    .d27(shift_register_1_q27), .q27(out_35), .d28(shift_register_1_q28), .q28(out_36),
    .d29(shift_register_1_q29), .q29(out_37), .d30(shift_register_1_q30), .q30(out_38),
    .d31(shift_register_1_q31), .q31(out_39));  // open: shift, in, out
  assign bit_extender_1_out = {{16{1'b0}}, register_1_q};  // Bit_Extender bit_extender_1
  Shifter #(.width(32)) shifter_1 (.in(bit_extender_1_out), .\dist (5'b10000), .out(shifter_1_out));
  assign bit_extender_2_out = {{16{1'b0}}, register_2_q};  // Bit_Extender bit_extender_2
  Adder #(.width(32)) adder_1 (.a(shifter_1_out), .b(bit_extender_2_out), .out(adder_1_out));  // open: cin, cout
  // Probe on adder_1_out
  // Probe on shift_register_1_q0
  // Probe on shift_register_1_q29
  // Probe on shift_register_1_q31

  // Other names for the same wires on the sheet: enRAM = GetData; rstOUT = Reset
endmodule
